// Logisim project control-logic.circ as structural Verilog: 1 circuit, main circuit control_logic
module control_logic (
  input  [31:0] Instruction,
  input  BrEq,
  input  BrLt,
  output PCSel,
  output RegWEn,
  output [2:0] ImmSel,
  output BrUn,
  output ASel,
  output BSel,
  output [3:0] ALUSel,
  output MemRW,
  output [1:0] WBSel
);

  wire and_1_out, and_2_out, and_3_out, and_4_out, Btype, comparator_4_eq, comparator_5_eq, comparator_6_eq,
       comparator_7_eq, or_1_out, RItype, Rtype;

  Comparator #(.width(5)) comparator_1 (.a(Instruction[6:2]), .b(5'b00100), .eq(RItype));  // open: gt, lt
  Comparator #(.width(5)) comparator_2 (.a(Instruction[6:2]), .b(5'b01100), .eq(Rtype));  // open: gt, lt
  Comparator #(.width(5)) comparator_3 (.a(Instruction[6:2]), .b(5'b11000), .eq(Btype));  // open: gt, lt
  Comparator #(.mode("unsigned"), .width(3)) comparator_4 (
    .a(Instruction[14:12]), .b(3'b101), .eq(comparator_4_eq));  // open: gt, lt
  Comparator #(.mode("unsigned"), .width(3)) comparator_5 (
    .a(Instruction[14:12]), .b(3'b000), .eq(comparator_5_eq));  // open: gt, lt
  and and_1 (and_1_out, Instruction[25], Rtype);
  Comparator #(.mode("unsigned"), .width(3)) comparator_6 (
    .a(Instruction[14:12]), .b(3'b101), .eq(comparator_6_eq));  // open: gt, lt
  or or_1 (or_1_out, comparator_4_eq, comparator_5_eq);
  and and_2 (and_2_out, Instruction[30], RItype, comparator_6_eq);
  and and_3 (and_3_out, Instruction[30], Rtype, or_1_out);
  or or_2 (ALUSel[3], and_2_out, and_3_out, and_1_out);
  Comparator #(.width(3)) comparator_7 (.a(Instruction[14:12]), .b(3'b000), .eq(comparator_7_eq));  // open: gt, lt
  or or_3 (RegWEn, 1'b0, Rtype, RItype);
  or or_4 (BSel, 1'b0, RItype);
  Multiplexer #(.width(3)) multiplexer_1 (.in0(Instruction[14:12]), .in1(3'b100), .out(ALUSel[2:0]), .sel(and_4_out));
  and and_4 (and_4_out, comparator_7_eq, Instruction[30]);
  or or_5 (WBSel[0], RItype, Rtype, 1'b0);
  or or_6 (WBSel[1], 1'b0, 1'b0);
  Priority_Encoder priority_encoder_1 (
    .in0(RItype), .in1(Btype), .out(ImmSel));  // open: in2, in3, in4, in5, in6, in7, en_in, gs, en_out

  assign ASel = 1'b0;
  assign BrUn = 1'b0;
  assign MemRW = 1'b0;
  assign PCSel = 1'b0;

  // Other names for the same wires on the sheet: opcode[4:0] = Instruction[6:2]; func3[2:0] = Instruction[14:12];
  //   func7[6:0] = Instruction[31:25]; func725 = Instruction[25]; func730 = Instruction[30]

  // Notes on the sheet:
  //   INPUTS to your circuit
  //   DON'T CHANGE THE LOCATIONS OF THE INPUTS AND OUTPUTS!
  //   OUTPUT from your circuit
endmodule
